// Logisim project DP_Project.circ as structural Verilog: 1 circuit, main circuit main
module main (
  input  in_1,
  input  [3:0] in_2,
  input  [2:0] in_3,
  input  in_4,
  input  [3:0] in_5,
  input  [2:0] in_6,
  input  [3:0] in_7,
  input  [2:0] in_8,
  input  [3:0] in_9,
  input  [1:0] in_10
);

  wire and_1_out, and_2_out, and_3_out, and_4_out, and_5_out, and_6_out, and_7_out, and_8_out, button_1_out,
       clock_1_out, or_1_out, or_2_out, t_ff_1_q;
  wire [1:0] counter_6_q;
  wire [2:0] counter_2_q, counter_4_q, counter_8_q;
  wire [3:0] counter_1_q, counter_3_q, counter_5_q, counter_7_q, n7_segment_display_1_p1,
       n7_segment_display_2_p3;

  Counter #(.max('hf), .width(4)) counter_1 (
    .clr(button_1_out), .load(and_3_out), .count(in_4), .clk(t_ff_1_q), .D(in_5), .Q(counter_1_q));  // open: up, carry
  Counter #(.max('h7), .width(3)) counter_2 (
    .clr(button_1_out), .load(and_1_out), .count(and_3_out), .clk(t_ff_1_q), .D(in_6), .Q(counter_2_q));  // open: up, carry
  Counter #(.max('hf), .width(4)) counter_3 (
    .clr(button_1_out), .load(and_2_out), .count(and_1_out), .clk(t_ff_1_q), .D(in_7), .Q(counter_3_q));  // open: up, carry
  Counter #(.max('h7), .width(3)) counter_4 (
    .clr(button_1_out), .load(and_4_out), .count(and_2_out), .clk(t_ff_1_q), .D(in_8), .Q(counter_4_q));  // open: up, carry
  Counter #(.max('hf), .width(4)) counter_5 (
    .clr(button_1_out), .load(or_1_out), .count(and_4_out), .clk(t_ff_1_q), .D(in_9), .Q(counter_5_q));  // open: up, carry
  or or_1 (or_1_out, and_5_out, and_6_out);
  Counter #(.max('h3), .width(2)) counter_6 (
    .clr(button_1_out), .load(and_6_out), .count(and_5_out), .clk(t_ff_1_q), .D(in_10), .Q(counter_6_q));  // open: up, carry
  Button button_1 (.out(button_1_out));
  and and_1 (and_1_out, and_3_out, counter_2_q[2], counter_2_q[0]);
  and and_2 (and_2_out, and_1_out, counter_3_q[3], counter_3_q[0]);
  or or_2 (or_2_out, and_7_out, and_8_out);
  Clock clock_1 (.out(clock_1_out));
  and and_3 (and_3_out, counter_1_q[0], counter_1_q[3]);
  and and_4 (and_4_out, and_2_out, counter_4_q[2], counter_4_q[0]);
  and and_5 (and_5_out, and_4_out, counter_5_q[3], counter_5_q[0]);
  and and_6 (and_6_out, and_4_out, counter_5_q[1], counter_5_q[0], counter_6_q[1]);
  Counter #(.max('hf), .width(4)) counter_7 (
    .clr(button_1_out), .load(or_2_out), .count(in_1), .clk(clock_1_out), .D(in_2), .Q(counter_7_q));  // open: up, carry
  T_Flip_Flop t_ff_1 (.T(and_7_out), .clk(clock_1_out), .Q(t_ff_1_q), .reset(button_1_out));  // open: Qn, preset
  Counter #(.max('h7), .width(3)) counter_8 (
    .clr(button_1_out), .load(and_7_out), .count(and_8_out), .clk(clock_1_out), .D(in_3), .Q(counter_8_q));  // open: up, carry
  and and_7 (and_7_out, counter_7_q[0], counter_7_q[1], counter_8_q[2], counter_8_q[1]);
  and and_8 (and_8_out, counter_7_q[3], counter_7_q[0]);
  // _7_Segment_Display 7_segment_display_1: pin names not known; wires that end beside it: n7_segment_display_1_p1, counter_5_q
  // BCD_to_7_Segment_decoder bcd_to_7_segment_decoder_1: pin names not known
  assign n7_segment_display_1_p1 = {{2{1'b0}}, counter_6_q};  // Bit_Extender bit_extender_1
  // _7_Segment_Display 7_segment_display_2: pin names not known; wires that end beside it: counter_5_q, t_ff_1_q, n7_segment_display_2_p3
  // _7_Segment_Display 7_segment_display_3: pin names not known; wires that end beside it: n7_segment_display_2_p3, counter_3_q
  // BCD_to_7_Segment_decoder bcd_to_7_segment_decoder_2: pin names not known
  // BCD_to_7_Segment_decoder bcd_to_7_segment_decoder_3: pin names not known
  _7_Segment_Display u_7_segment_display_4 ();  // open: g, f, a, b, e, d, c, dp
  // BCD_to_7_Segment_decoder bcd_to_7_segment_decoder_4: pin names not known
  assign n7_segment_display_2_p3 = {{1{1'b0}}, counter_4_q};  // Bit_Extender bit_extender_2
endmodule
